# Fritzing sketch nke69 - arduino - raspberry (saved by Fritzing 0.9.3b)
breadboards: 1

parts:
  arduino_uno_rev3 = Arduino Uno (Rev3)
  LCD_16X2_standard = LCD screen
  Potmeter_LCD = Trimmer Potentiometer [maximum_resistance=10kΩ part_number="Potmeter LCD" package=THT]
  R1 = Resistor [tolerance=±5% resistance=220 package=THT]
  Water_Level = LED - 5mm [color="Blue (430nm)" package="5 mm [THT]"]
  R2 = Resistor [tolerance=±5% resistance=220 package=THT]
  R3 = Resistor [tolerance=±5% resistance=220 package=THT]
  pH_High = LED - 5mm [color="Yellow (592nm)" package="5 mm [THT]"]
  R4 = Resistor [tolerance=±5% resistance=10k package=THT]
  R5 = Resistor [tolerance=±5% resistance=4.7k package=THT]
  C1 = Ceramic Capacitor [capacitance=0.22mF package="0805 [SMD, multilayer]"]
  DS10 = DS18B20 1-Wire Temperature Sensor Probe Cable
  220AC1 = Lilypad Battery Connect
  220AC2 = Lilypad Battery Connect
  220AC3 = Lilypad Battery Connect
  220AC4 = Lilypad Battery Connect
  Raspberry_Pi_4 = Raspberry Pi 3 [part_number=RPI-3-V1.2]
  M1 = DC Motor [part_number="Lampe du meuble"]
  M2 = DC Motor [part_number=Chauffage]
  M3 = DC Motor [part_number=Brassage]
  M4 = DC Motor [part_number="Pompe à air"]
  RPICam_to_Pi_with_CSI_Cable1 = TRANSCHIPTC5747 [package=camera_sfv24r-2st_2]  # not connected
  Relais_1 = 4-Channel 5v Relay Shield [package=relay-4ch5v10a]
  R6 = Resistor [tolerance=±5% resistance=220 package=THT]
  Heat_Low = LED - 5mm [color="Green (565nm)" package="5 mm [THT]"]
  S1 = SWITCH-MOMENTARY-2 [package=reed_switch_plastic]
  Relais_2 = 4-Channel 5v Relay Shield [package=relay-4ch5v10a]
  Capteur_de_porte = LilyPad Light Sensor
  Temp_Min = POT [package=3362u]
  Temp_Max = POT [package=3362u]
  Set_pH_Value = POT [package=3362u]
  R7 = Resistor [tolerance=±5% resistance=220 package=THT]
  Heat_High = LED - 5mm [color="Red (633nm)" package="5 mm [THT]"]
  R8 = Resistor [tolerance=±5% resistance=4.7k package=THT]
  DHT2 = DHT22 Humidity and Temperature Sensor
  C2 = Electrolytic Capacitor [capacitance=10μF voltage=50V package="0605 [SMD, electrolytic]"]
  S2 = PH meter [part_number="Sonde PH SKU - SEN0161 avec pH meter" package=THT]
  220AC5 = Lilypad Battery Connect
  220AC6 = Lilypad Battery Connect
  220AC7 = Lilypad Battery Connect
  220AC8 = Lilypad Battery Connect
  M5 = DC Motor [part_number="Réserve 2"]
  M6 = DC Motor [part_number="Réserve 1"]
  M7 = DC Motor [part_number=Osmolateur]
  M8 = DC Motor [part_number=Cooler]
  S3 = PH meter [part_number="Sonde EC - DIY ;)" package=THT]
  R9 = Resistor [tolerance=±5% resistance=10k package=THT]
  R10 = Resistor [tolerance=±5% resistance=220 package=THT]

nets:
  N1: arduino_uno_rev3.A0, S3.pin3, R9.Pin_1
  N2: arduino_uno_rev3.A1, Temp_Min.S
  N3: arduino_uno_rev3.A2, Temp_Max.S
  N4: arduino_uno_rev3.A3, S2.pin1
  N5: arduino_uno_rev3.A4/SDA, Set_pH_Value.S
  N6: arduino_uno_rev3.A5/SCL, R6.Pin_1, Heat_Low.anode
  N7: arduino_uno_rev3.D8, Water_Level.anode, R3.Pin_0
  N8: arduino_uno_rev3.D9_PWM, R5.Pin_1, DS10.DQ
  N9: arduino_uno_rev3.D10_PWM/SS, R2.Pin_1, pH_High.anode
  N10: arduino_uno_rev3.D11_PWM/MOSI, LCD_16X2_standard.E
  N11: arduino_uno_rev3.D12/MISO, LCD_16X2_standard.RS
  N12: arduino_uno_rev3.D13/SCK, R10.Pin_0
  N13: arduino_uno_rev3.D2, LCD_16X2_standard.DB7
  N14: arduino_uno_rev3.D3_PWM, LCD_16X2_standard.DB6
  N15: arduino_uno_rev3.D4, LCD_16X2_standard.DB5
  N16: arduino_uno_rev3.D5_PWM, LCD_16X2_standard.DB4
  N17: arduino_uno_rev3.D6_PWM, R7.Pin_1, Heat_High.anode
  N18: arduino_uno_rev3.D7, R4.Pin_1, S1.1
  N19: arduino_uno_rev3.RESET, C2.+
  VDD: arduino_uno_rev3.5V, LCD_16X2_standard.VDD, LCD_16X2_standard.LED+, Potmeter_LCD.leg1, R5.Pin_0, C1.1, DS10.VDD, S1.2, Temp_Min.E, Temp_Max.E, Set_pH_Value.E, R8.Pin_0, DHT2.VDD, S2.pin2
  GND: arduino_uno_rev3.GND, LCD_16X2_standard.VSS, LCD_16X2_standard.R/W, Potmeter_LCD.leg2, R1.Pin_1, Water_Level.cathode, R2.Pin_0, R3.Pin_1, pH_High.cathode, R4.Pin_0, C1.0, DS10.GND, R6.Pin_0, Heat_Low.cathode, Temp_Min.A, Temp_Max.A, Set_pH_Value.A, R7.Pin_0, Heat_High.cathode, DHT2.GND, C2.-, S2.pin3, R9.Pin_0
  N20: LCD_16X2_standard.V0, Potmeter_LCD.wiper
  N21: LCD_16X2_standard.LED-, R1.Pin_0
  N22: 220AC1.-, Relais_1.K3-On
  N23: 220AC1.+, M2.pin_2
  N24: 220AC2.-, Relais_1.K4-On
  N25: 220AC2.+, M1.pin_2
  N26: 220AC3.-, Relais_1.K2-On
  N27: 220AC3.+, M3.pin_2
  N28: 220AC4.-, Relais_1.K1-On
  N29: 220AC4.+, M4.pin_2
  GND_2: Raspberry_Pi_4.GND, Relais_1.GND, Relais_2.GND, Capteur_de_porte.-
  N30: Raspberry_Pi_4.GPIO17, Relais_1.IN2
  N31: Raspberry_Pi_4.GPIO27, Capteur_de_porte.+
  N32: Raspberry_Pi_4.GPIO22, R8.Pin_1, DHT2.DATA
  N33: Raspberry_Pi_4.GPIO5, Relais_2.IN1
  N34: Raspberry_Pi_4.GPIO6, Relais_2.IN2
  N35: Raspberry_Pi_4.GPIO13, Relais_2.IN3
  N36: Raspberry_Pi_4.GPIO21, Relais_1.IN4
  N37: Raspberry_Pi_4.GPIO20, Relais_1.IN3
  N38: Raspberry_Pi_4.GPIO18, Relais_1.IN1
  VCC: Raspberry_Pi_4.5V, Relais_1.VCC, Relais_2.VCC
  N39: M1.pin_1, Relais_1.K4-Off
  N40: M2.pin_1, Relais_1.K3-Off
  N41: M3.pin_1, Relais_1.K2-Off
  N42: M4.pin_1, Relais_1.K1-Off
  N43: Relais_2.K1-Off, M8.pin_1
  N44: Relais_2.K1-On, 220AC8.-
  N45: Relais_2.K2-Off, M7.pin_1
  N46: Relais_2.K2-On, 220AC7.-
  N47: Relais_2.K3-Off, M6.pin_1
  N48: Relais_2.K3-On, 220AC5.-
  N49: Relais_2.K4-Off, M5.pin_1
  N50: Relais_2.K4-On, 220AC6.-
  N51: 220AC5.+, M6.pin_2
  N52: 220AC6.+, M5.pin_2
  N53: 220AC7.+, M7.pin_2
  N54: 220AC8.+, M8.pin_2
  N55: S3.pin2, R10.Pin_1

notes:
  Capteur de Niveau Read
  0 ou 1
  condensateur 22nf afin de ne pas avoir d'interférence avec l'écran LCD lorsque les relais active ou désactive le 220V
  Relais 1
  ------------------------------
  PIN4 : 5VCC ROUGE
  PIN6 : GROUND NOIR
  PIN11 GPIO18 VERT IN1
  PIN12 GPIO17 BLEU IN2
  PIN38 GPIO 20 ORANGE IN3
  PIN40 GPIO21 GRIS IN4
  Relais 2
  ------------------------------
  PIN2 : 5VCC ROUGE
  PIN14 : GROUND NOIR
  PIN29 GPIO5 VERT IN1
  PIN31 GPIO6 BLEU IN2
  PIN33 GPIO13 ORANGE IN3
  PIN35 GPIO19 GRIS IN4
  PIN13 GPIO27 BLANC
  PIN9 GND NOIR
  capacitor 10uF pour desactiver le reset du port Com de l'arduino
  DHT22 (raspberry)
  resistance 4.7K
  GPIO22 PIN 15

custom parts:
  4-Channel 5v Relay Shield: 4 Channel 5v Relay Shield w. 2x SPD-06VDC-SD-C

// code stored in the sketch: aquarium_temp_low_high_met_pH.ino


#include <LiquidCrystal.h>
#include <OneWire.h>

 int DS18S20_Pin = 9; //DS18S20 Signal pin on digital 9
LiquidCrystal lcd(12, 11, 5, 4, 3, 2); // pins use for LCD

int val, phset; 

int utemp=0, dtemp=0, valup=0, valdown=0;
//Temperature chip i/o
 OneWire ds(DS18S20_Pin);  // ds18b20 on digital pin 9 or change to your ditial pin number
           
const int dtempPin = A1;                   //Lower Limit pin
const int utempPin = A2;                   //Upper limit pin
#define phsetPin A4 
const int waterPin = 7;
const int ledup = 6;                      //led warn temp upper limit or Fan relais
const int ledph = 10;
const int ledwater = 8;
#define SensorPin A3          //pH meter Analog output to Arduino Analog Input 3
#define Offset 0.17 
unsigned long int avgValue;  //Store the average value of the sensor feedback
float b;
int buf[10],temp;





void setup() 
{
  lcd.begin(16,2); 
 
  pinMode(ledup,OUTPUT);
  pinMode(ledph,OUTPUT);
  pinMode(utempPin, INPUT);
  pinMode(dtempPin, INPUT); 
  pinMode(phsetPin, INPUT);
  pinMode(waterPin, INPUT);
  pinMode(ledwater,OUTPUT);
  const int phsetPin = A4;
  int waterlevel;
digitalWrite(ledup,HIGH);
}


void loop()

{


  {

  float temperature = getTemp();
    utemp= analogRead(utempPin);
    dtemp= analogRead(dtempPin);
   float phset = analogRead(phsetPin);

    utemp=map(utemp, 0, 1023, 19, 31);
    dtemp=map(dtemp, 0, 1023, 19, 31);
    phset=map(phset, 0.0, 1023.0, 10.0, 140.0);
    phset=(phset/10);
      for(int i=0;i<10;i++)       //Get 10 sample value from the sensor for smooth the value
  { 
    buf[i]=analogRead(SensorPin);
    delay(10);
  }
  for(int i=0;i<9;i++)        //sort the analog from small to large
  {
    for(int j=i+1;j<10;j++)
    {
      if(buf[i]>buf[j])
      {
        temp=buf[i];
        buf[i]=buf[j];
        buf[j]=temp;
      }
    }
  }
  avgValue=0;
  for(int i=2;i<8;i++)                      //take the average value of 6 center sample
    avgValue+=buf[i];
  float phValue=(float)avgValue*5.0/1024/6; //convert the analog into millivolt
  phValue=3.5*phValue+Offset;                      //convert the millivolt into pH value
 
          int waterlevel;
   waterlevel=digitalRead(waterPin); 
   
if (waterlevel == HIGH)
{
digitalWrite(ledwater,HIGH);
 lcd.clear();
 lcd.print("WATERPEIL LAAG");
 lcd.setCursor(0, 1);                     
  lcd.print("BIJVULLEN AUB");
  
delay(1500);
}
else
{
digitalWrite(ledwater,LOW);
}

    if (getTemp() >utemp)  
  { 
 
    
 digitalWrite(ledup,LOW);
      lcd.clear();
       


lcd.setCursor(0, 0); 
lcd.print("TEMP:");
    lcd.setCursor(5, 0);                       
    lcd.print(getTemp(),1); 

    lcd.setCursor(10,0);
    lcd.print("pH=");
    lcd.setCursor(13,0);
    lcd.print(phValue,1);
    lcd.setCursor(2,1);  
    lcd.print(utemp);
    lcd.setCursor(5,1);                 
    lcd.print("L:");
lcd.setCursor(7,1);
    lcd.print(dtemp);
    lcd.setCursor(10,1);
    lcd.print("? ");
      lcd.setCursor(0, 1);                     
  lcd.print("H:");
    lcd.setCursor(12,1);
    lcd.print(phset,1);
  
   delay(100);
     
 
     
     
       if (phValue > phset)
  {
    digitalWrite(ledph,LOW);
  }
  else
  {
    digitalWrite(ledph,HIGH);
  }
 delay(200); 

           
   } 
   else if (getTemp() <= utemp && getTemp() >= dtemp && waterlevel == LOW)
   {

      lcd.clear();
       


lcd.setCursor(0, 0); 
lcd.print("TEMP:");
    lcd.setCursor(5, 0);                       
    lcd.print(getTemp(),1); 

    lcd.setCursor(10,0);
    lcd.print("pH=");
    lcd.setCursor(13,0);
    lcd.print(phValue,1);
    lcd.setCursor(2,1);  
    lcd.print(utemp);
    lcd.setCursor(5,1);                 
    lcd.print("L:");
lcd.setCursor(7,1);
    lcd.print(dtemp);
    lcd.setCursor(10,1);
    lcd.print("? ");
      lcd.setCursor(0, 1);                     
  lcd.print("H:");
    lcd.setCursor(12,1);
    lcd.print(phset,1);
  
   delay(100);
   
  {
 if (phValue > phset)
  {
   digitalWrite(ledph,LOW);
  }
  else
  {
    digitalWrite(ledph,HIGH);
  }
} 

   }
      else if (getTemp() < dtemp)  
  {  
 
    
 digitalWrite(ledup,HIGH); 
      lcd.clear();
       


lcd.setCursor(0, 0); 
lcd.print("TEMP:");
    lcd.setCursor(5, 0);                       
    lcd.print(getTemp(),1); 
 ;
    lcd.setCursor(10,0);
    lcd.print("pH=");
    lcd.setCursor(13,0);
    lcd.print(phValue,1);
    lcd.setCursor(2,1);  
    lcd.print(utemp);
    lcd.setCursor(5,1);                 
    lcd.print("L:");
lcd.setCursor(7,1);
    lcd.print(dtemp);
    lcd.setCursor(10,1);
    lcd.print("? ");
      lcd.setCursor(0, 1);                     
  lcd.print("H:");
    lcd.setCursor(12,1);
    lcd.print(phset,1);
  
   delay(100);
     



           
   } 
   
  }
  
}
float getTemp(){
   //returns the temperature from one DS18S20 in DEG Celsius

   byte data[12];
   byte addr[8];

   if ( !ds.search(addr)) {
       //no more sensors on chain, reset search
       ds.reset_search();
       return -1000;
   }

   if ( OneWire::crc8( addr, 7) != addr[7]) {
       Serial.println("CRC is not valid!");
       return -1000;
   }

   if ( addr[0] != 0x10 && addr[0] != 0x28) {
       Serial.print("Device is not recognized");
       return -1000;
   }

   ds.reset();
   ds.select(addr);
   ds.write(0x44,1); // start conversion, with parasite power on at the end

   byte present = ds.reset();
   ds.select(addr);   
   ds.write(0xBE); // Read Scratchpad

  
   for (int i = 0; i < 9; i++) { // we need 9 bytes
     data[i] = ds.read();
   }
  
   ds.reset_search();
  
   byte MSB = data[1];
   byte LSB = data[0];

   float tempRead = ((MSB << 8) | LSB); //using two's compliment
   float TemperatureSum = tempRead / 16;
  
   return TemperatureSum;
}

// code stored in the sketch: aquarium_temp_low_high_met_pH_hans.ino
//   ///Aquarium temperature (heating and cooling)) and pH- controller and waterlevel indicator///
    //controls a cooling-fan,aquarium-heater and co2 system magnet valve.
    // i used a 4 relais board,used 3 relais
    // make sure the relais-board has its own power-source (1x power adapter 12volt 1 amp,and 2x 7805 5 volt regulator
   // 1x 7805 for arduino pro mini and sensors and and lcd, 1x 7805 for relais-board.
   
   //parts list:
   
   // ph sensor  PH meterSKU: SEN0161.amplifier board incluided.
   // 4 channel relais board.
   // 3x potmeter 10 k for phset,maxtempset and mintempset.
   // 1x trimpot 10 k for lcd-contrast.
   // 1x 16x2 lcd.
   // 1x power adapter 12 volt 1 amp.
   // powerplug for housing to connect transformer to.
   // 2x 7805 volt regulator ,make a small pcb board with those two and the needed capacitors.
   // 1x arduino pro mini 16 mhz 5 volts with atmega 328.
   // 1x led or blinkled
   // 1x 3 screw connector for temp sensor, 1x 2 screw connector for float switch sensor
   // float sensor switch Water Level Liquid Sensor example;  http://www.ebay.ca/itm/160618121548
   // 2x build-on wall sockets ,here controlled by two relais,1 for heater and 1 for magnetvalve,both on 220 volts.
   // 1x pushbutton,connected to reset.
   // sometimes lcd can get scrambled because of the relais switching, 1 push on reset to fix it.
   // if lcd is crambled the controller still work properly,lcd is just for indication!!!
   // when reset,there is no indication of the co2  status "on or s@" on the lcd,that picks up automaticly when it changes.
   // a nice housing of your choice
   
   // take a piece of pcb board to drill 5 holes at the right distance next to each other in the housing and put a 5 pin header
   // through it with the pins to the outside!!,connect the pro mini on the inside for re-programming without
   // the need to open your housing.just connect the usb to TTL converter to the 5 pins,mark the ground pin for right connection.
   
   // For the temp sensor and the floatsensor i used screw connectors on the outside of the housing. 
   
   
   
#include <LiquidCrystal.h>
#include <OneWire.h>

int DS18S20_Pin = 9; //DS18S20 Signal pin on digital 9 temp sensor
LiquidCrystal lcd(12, 11, 5, 4, 3, 2); // pins use for LCD16x2

int val, phset; 

int utemp=0, dtemp=0, valup=0, valdown=0;
//Temperature chip i/o
OneWire ds(DS18S20_Pin);  // ds18b20 on digital pin 9 or change to your ditial pin number

const int dtempPin = A1;                   //Lower temp.Limit pin with potmeter
const int utempPin = A2;                   //Upper temp.limit pin with potmeter
#define phsetPin A4                        //set desired ph-value with potmeter
const int waterPin = 7;                   //floatswitch  for waterlevel
const int ledup = 6;                      //led warning temp. upper limit or cooling Fan relais!
const int ledph = 10;                     //led warning ph or relais for magnetic valve co2-system
const int ledwater = 8;       //warning led for water level
const int heat = 13;          //relais heater element
#define SensorPin A3          //pH meter Analog output to Arduino Analog Input 3
#define Offset 0.2    //set your offset ph sensor here!!! shorted then ph=7 ,here mine gives 6.8 so offset = 0.2
unsigned long int avgValue;  //Store the average value of the sensor feedback
float b;
int buf[10],temp;





void setup() 
{
  lcd.begin(16,2); 

  digitalWrite(ledup, HIGH);  // relais off !! depends on relais board 
  digitalWrite(ledph, HIGH);
  digitalWrite(heat, HIGH);
  pinMode(ledup,OUTPUT);
  pinMode(ledph,OUTPUT);
  pinMode(heat,OUTPUT);
  pinMode(utempPin, INPUT);
  pinMode(dtempPin, INPUT); 
  pinMode(phsetPin, INPUT);
  pinMode(waterPin, INPUT);
  pinMode(ledwater,OUTPUT);
  const int phsetPin = A4;
  int waterlevel;


}


void loop()

{


  {

    float temperature = getTemp();    // get temp from tempsensor
    utemp= analogRead(utempPin);      // get max set temp from potmeter
    dtemp= analogRead(dtempPin);      // get min set temp from potmeter
    float phset = analogRead(phsetPin);    // get desired ph value from potmeter

    utemp=map(utemp, 0, 1023, 19, 31);   // you can change 19 and 31 to your desired temp range for the set potmeter
    dtemp=map(dtemp, 0, 1023, 19, 31);   // idem
    phset=map(phset, 0.0, 1023.0, 10.0, 140.0);  // give the ph value
    phset=(phset/10);                            // with 1 decimal
    for(int i=0;i<10;i++)       //Get 10 sample value from the sensor for smooth the value
    { 
      buf[i]=analogRead(SensorPin);
      delay(10);
    }
    for(int i=0;i<9;i++)        //sort the analog from small to large
    {
      for(int j=i+1;j<10;j++)
      {
        if(buf[i]>buf[j])
        {
          temp=buf[i];
          buf[i]=buf[j];
          buf[j]=temp;
        }
      }
    }

    avgValue=0;
    for(int i=2;i<8;i++)                      //take the average value of 6 center sample
      avgValue+=buf[i];
    float phValue=(float)avgValue*5.0/1024/6; //convert the analog into millivolt
    phValue=3.5*phValue+Offset;                      //convert the millivolt into pH value

    int waterlevel;
    waterlevel=digitalRead(waterPin); 

    if (waterlevel == HIGH)
    {

      digitalWrite(ledwater,HIGH); //led on ,i used a blinkled
      lcd.setCursor(0,1);
      lcd.print("^^WATER NIVEAU^^");   //water level  ,total of 16 characters incluiding tab
      delay(500);                      //change switchingspeed to your liking
      lcd.setCursor(0,1);              // replace on same position
      lcd.print("______LAAG______");   //low  ,again total of 16 characters
      delay(500);                      // again change to your liking

    }
    else
    {
      digitalWrite(ledwater,LOW); //led off
      lcd.setCursor(0, 0); 
      lcd.print("TEMP:");
      lcd.setCursor(5, 0);                       
      lcd.print(getTemp(),1); // temp with 1 decimal
      lcd.setCursor(10,0);
      lcd.print("pH:");
      lcd.setCursor(13,0);
      lcd.print(phValue,1);     // ph value with 1 decimal
      lcd.setCursor(2,1);  
      lcd.print(utemp);         //max set temp,no decimal
      lcd.setCursor(4,1);                 
      lcd.print(" ");
      lcd.setCursor(5,1);                 
      lcd.print("L~");   // L from Low set temp with arrow right
      lcd.setCursor(7,1);
      lcd.print(dtemp);     //min set temp ,no decimal
      lcd.setCursor(12,1);
      lcd.print("~");   //this sign gives on my lcd an arrow to the right
      lcd.setCursor(0, 1);                     
      lcd.print("H~");   //H from High set temp with arrow right
      lcd.setCursor(13,1);
      lcd.print(phset,1);  //ph set value with 1 decimal
      lcd.setCursor(9,1);                 
      lcd.print(" ");
      delay(20);
    }

    if (getTemp() > dtemp+(utemp-dtemp))  //temp higher than max set temp
    { 
      digitalWrite(ledup,LOW);  //cooling fan on
      delay(10); 
    }

    if (getTemp() <= dtemp)  //temp lower or equal than min set temp
    {  
      digitalWrite(ledup,HIGH); //cooling fan off
      delay(10);
    }

    if (getTemp() < dtemp-0.1)  // temp lower than 0.1 degrees-celsius below min set temp
    {
      digitalWrite(heat,LOW);    // heater on
      lcd.setCursor(9, 0); 
      lcd.print("*");  // sign heater=on
      delay(300);
      lcd.setCursor(9, 0);
      lcd.print(" ");   // no sign heater=off
      delay(300);
    }

    if (getTemp() >= dtemp+0.2)    //temp higher than 0.2 degrees-celsius above min set temp
    {
      digitalWrite(heat, HIGH);    //heater off
      delay(10);
      lcd.setCursor(9, 0); 
      lcd.print(" ");
    }






    if (phValue > phset+0.05)    // offset 0.05  ph is allowed to rise above the set ph value before before switching on co2 or led
    {
      digitalWrite(ledph,LOW);   // magnetvalve co2 open,or led on
      delay(10);
      lcd.setCursor(10,1);
      lcd.print("ON"); // co2 or led = on  
      delay(5);



    }
    else

        if (phValue <= phset)
      {
        digitalWrite(ledph,HIGH);  //magnetvalve co2 closed, or led off
        delay(10);
        lcd.setCursor(10,1);
        lcd.print("s@");  // co2 or led equal or below ph set , S AT or "set"
        delay(5);

      }

  } 

}





float getTemp(){
  //returns the temperature from one DS18S20 in DEG Celsius

  byte data[12];
  byte addr[8];

  if ( !ds.search(addr)) {
    //no more sensors on chain, reset search
    ds.reset_search();
    return -1000;
  }

  if ( OneWire::crc8( addr, 7) != addr[7]) {
    Serial.println("CRC is not valid!");
    return -1000;
  }

  if ( addr[0] != 0x10 && addr[0] != 0x28) {
    Serial.print("Device is not recognized");
    return -1000;
  }

  ds.reset();
  ds.select(addr);
  ds.write(0x44,1); // start conversion, with parasite power on at the end

  byte present = ds.reset();
  ds.select(addr);   
  ds.write(0xBE); // Read Scratchpad


  for (int i = 0; i < 9; i++) { // we need 9 bytes
    data[i] = ds.read();
  }

  ds.reset_search();

  byte MSB = data[1];
  byte LSB = data[0];

  float tempRead = ((MSB << 8) | LSB); //using two's compliment
  float TemperatureSum = tempRead / 16;

  return TemperatureSum;
}

// code stored in the sketch: aquariumcontrollerFinaliconsblink.ino
/*********************************************************************
   FishPiNo.ino
   Hardware platform   : Arduino Or Arduino Mega2560

   Description:
   Aquarium temperature (heating and cooling)) and pH-controller.
   Waterlevel indicator controls a cooling-fan, aquarium-heater and co2 system magnet valve.
   LCD Display for alert and views.

   Sensor pin:

   DIGITAL:
   LCD            : D2 - D3 - D4 - D5 - D11 - D12
   LEDUP          : D6  //led warning temp. upper limit or cooling Fan relais!
   WATERPIN       : D7  //floatswitch  for waterlevel
   LEDWATER       : D8  //warning led for water level
   DS18B20        : D9  // Signal pin on digital 9 temp sensor
   LEDPH          : D10 //led warning ph or relais for magnetic valve co2-system
   HEATER         : D13 //RELAY FOR HEATER

   ANALOG:
   dtempPin       : A1  //Lower temp.Limit pin with potmeter
   utempPin       : A2  //Upper temp.limit pin with potmeter
   phsetPin       : A4  //set desired ph-value with potmeter
   SensorPin PH   : A3  //pH meter Analog output to Arduino Analog Input 3

   Free PIN:
   A0 - A5


   Author  :  nke69(nookie69@gmail.com)
   Version :  V1.0
   Date    :  31-03-2018

 Explanation :
 
 Aquarium temperature (heating and cooling)) and pH- controller and waterlevel indicator controls a cooling-fan,aquarium-heater and co2 system magnet valve.///
 i used a 4 relais board,used 3 relais so you can do without the 3 leds.(those were for testing).
 make sure the relais-board has its own power-source (1x power adapter 12volt 1 amp,and 2x 7805 5 volt regulator
 1x 7805 for arduino pro mini and sensors and and lcd, 1x 7805 for relais-board.

 Parts list:

 ph sensor  PH meterSKU: SEN0161.amplifier board incluided.
 DS18B20 one wire digital temperatur sensor,watersealed.
 4 channel relais board.5 volts
 3x potmeter 10 k for phset,maxtempset and mintempset.
 1x trimpot 10 k for lcd-contrast.
 1x 16x2 lcd.
 1x power adapter 12 volt 1 amp.
 powerplug for housing to connect poweradapter to.
 2x 7805 volt regulator ,make a small pcb board with those two and the needed capacitors,to make 2 seperated 5 volts supplies,
 one for the relais board,one for the rest.
 1x arduino pro mini 16 mhz 5 volts with atmega 328.
 1x led or blinkled for waterlevel warning indicator.
 1x 3 screw connector for temp sensor, 1x 2 screw connector for float switch sensor
 float sensor switch Water Level Liquid Sensor example;  http://www.ebay.ca/itm/160618121548
 2x build-on wall sockets ,both on 220 volts mains,here controlled by two relais,1 for heater and 1 for magnetvalve.
 1x pushbutton,connected to reset.

 Tips:

 Sometimes lcd can get scrambled because of the relais switching or the switching of my TL lighting, 1 push on //reset to fix it.
 a small condenator (100nF-10uF,trial and error) directly soldered over the lcd power pins(VSS and VDD) might help.
 if lcd is crambled the controller still work properly,lcd is just for indication!!!
 a nice housing of your choice

 take a piece of pcb experimentboard as a mask to drill 5 holes at the right distance next to each other in the housing and put a 5 //pin header
 through it with the pins to the outside!!,connect the pro mini on the inside for re-programming without
 the need to open your housing.just connect the usb to TTL converter to the 5 pins,mark the ground pin for right //connection.
 For the temp sensor and the floatsensor i used the screw connectors on the outside of the housing. 
 make sure you have the libraries LiquidCrystal.h and OneWire.h installed in the arduino IDE.

 **********************************************************************/

#include <Adafruit_Sensor.h>
#include <LiquidCrystal.h>
#include <OneWire.h>

/*DS18S20 Signal pin on digital 9 temp sensor , change to your digital pin number*/
int DS18S20_Pin = 9;

// pins use for LCD16x2
LiquidCrystal lcd(12, 11, 5, 4, 3, 2);

int val, phset;
int state;

int utemp = 0, dtemp = 0, valup = 0, valdown = 0;
//Temperature chip i/o
OneWire ds(DS18S20_Pin);     // ds18b20 on digital pin 9
const int dtempPin = A1;     //Lower temp.Limit pin with potmeter
const int utempPin = A2;     //Upper temp.limit pin with potmeter
#define phsetPin A4          //set desired ph-value with potmeter
const int waterPin = 7;      //floatswitch  for waterlevel
const int ledup = 6;         //led warning temp. upper limit or cooling Fan relais!
const int ledph = 10;        //led warning ph or relais for magnetic valve co2-system
const int ledwater = 8;      //warning led for water level
const int heat = 13;         //relais heater element
#define SensorPin A3         //pH meter Analog output to Arduino Analog Input 3
#define Offset 0.0           //set your offset ph sensor here!!! shorted then ph=7 ,here mine gives 6.8 so offset = 0.2
unsigned long int avgValue;  //Store the average value of the sensor feedback
float b;
int buf[10], temp;
byte flame[8] = {B00100, B00100, B01110, B01010, B11011, B10001, B10001, B01110};       //icon for flame
byte smalflame[8] = {B00000, B00000, B00100, B00100, B01110, B01010, B10001, B01110};   //icon for small flame
byte thermometer[8] = {B00100, B01010, B01110, B01110, B11111, B11111, B11111, B01110}; //icon thermometer
byte celsius[8] = {B11100, B10100, B11100, B00000, B00000, B00000, B00000, B00000};     //icon celsius
byte tank[8] = {B01100, B00010, B00111, B01101, B10101, B10111, B10111, B00111};        //icon co2 tank
byte co2[8] = {B00001, B00100, B10001, B00100, B01010, B00001, B00010, B00001};         //icon c02 spray
void setup()
{
  Serial.begin(9600);
  lcd.begin(16, 2);
  lcd.createChar(1, flame);
  lcd.createChar(2, smalflame);
  lcd.createChar(3, thermometer);
  lcd.createChar(4, celsius);
  lcd.createChar(5, tank);
  lcd.createChar(6, co2);

  pinMode(ledup, OUTPUT);
  pinMode(ledph, OUTPUT);
  /*pinMode(heat, OUTPUT);*/
  pinMode(utempPin, INPUT);
  pinMode(dtempPin, INPUT);
  pinMode(phsetPin, INPUT);
  pinMode(waterPin, INPUT);
  pinMode(ledwater, OUTPUT);
  const int phsetPin = A4;
  int waterlevel;
  digitalWrite(ledup, HIGH);  // relais off !! depends on relais board you have.
  digitalWrite(ledph, HIGH);
  digitalWrite(heat, HIGH);
  state == HIGH ; // heat sign off
}

void loop()

{
  {
    float temperature = getTemp();                  // get temp from tempsensor
    utemp = analogRead(utempPin);                   // get max set temp from potmeter
    dtemp = analogRead(dtempPin);                   // get min set temp from potmeter
    float phset = analogRead(phsetPin);             // get desired ph value from potmeter

    utemp = map(utemp, 0, 1023, 19, 31);            // you can change 19 and 31 to your desired temp range for the set potmeter
    dtemp = map(dtemp, 0, 1023, 19, 31);            // idem
    phset = map(phset, 0.0, 1023.0, 10.0, 140.0);   // give the ph value
    phset = (phset / 10);                           // with 1 decimal
    for (int i = 0; i < 10; i++)                    //Get 10 sample value from the sensor for smooth the value
    {
      buf[i] = analogRead(SensorPin);
      delay(10);
    }
    for (int i = 0; i < 9; i++) //sort the analog from small to large
    {
      for (int j = i + 1; j < 10; j++)
      {
        if (buf[i] > buf[j])
        {
          temp = buf[i];
          buf[i] = buf[j];
          buf[j] = temp;
        }
      }
    }

    avgValue = 0;
    for (int i = 2; i < 8; i++)                       //take the average value of 6 center sample
      avgValue += buf[i];
    float phValue = (float)avgValue * 5.0 / 1024 / 6; //convert the analog into millivolt
    phValue = 3.5 * phValue + Offset;                 //convert the millivolt into pH value

    int waterlevel;
    waterlevel = digitalRead(waterPin);

    if (waterlevel == HIGH)
    {

      digitalWrite(ledwater, HIGH);     //led on ,i used a blinkled
      lcd.setCursor(0, 1);
      lcd.print("^^^NIVEAU EAU^^^");    //water (niveau=)level  ,total of 16 characters incluiding tab
      Serial.print("Niveau de l'eau");
      delay(500);                       //change switchingspeed to your liking
      lcd.setCursor(0, 1);              // replace on same position
      lcd.print("____TROP BAS____");    //(laag=)low  ,again total of 16 characters
      Serial.print("BAS");
      delay(500);                       // again change to your liking

    }
    else
    {
      digitalWrite(ledwater, LOW); //led off
      lcd.setCursor(0, 0);
      lcd.print(char(3));
      lcd.setCursor(1, 0);
      lcd.print(getTemp(), 1);    // temp with 1 decimal
      lcd.setCursor(5, 0);
      lcd.print(char(4));
      lcd.setCursor(6, 0);
      lcd.print("C");
      lcd.setCursor(10, 0);
      lcd.print("pH:");
      lcd.setCursor(13, 0);
      lcd.print(phValue, 1);      // ph value with 1 decimal
      lcd.setCursor(7, 1);
      lcd.print(utemp);           //max set temp,no decimal
      lcd.setCursor(4, 1);
      lcd.print(" ");
      lcd.setCursor(0, 1);
      lcd.print("L~");            // L from Low set temp with arrow right
      lcd.setCursor(2, 1);
      lcd.print(dtemp);           //min set temp ,no decimal
      lcd.setCursor(12, 1);
      lcd.print("~");             //this sign gives on my lcd an arrow to the right
      lcd.setCursor(5, 1);
      lcd.print("H~");            //H from High set temp with arrow right
      lcd.setCursor(13, 1);
      lcd.print(phset, 1);        //ph set value with 1 decimal
      lcd.setCursor(9, 1);
      lcd.print(" ");
      lcd.setCursor(10, 1);
      lcd.print(char(5));
      delay(20);
      Serial.print("Temperature :");
      Serial.println(getTemp(), 1);
      Serial.print("PH :");
      Serial.println(phValue, 1);
      Serial.print("Niveau d'eau :");
      Serial.println(waterlevel);
      Serial.println("");
      state = digitalRead(heat); // read the state of the heater-relais(when reset,the heatersign would turn on while heater is off.This gives the right indication.)
    }

    if (getTemp() > dtemp + (utemp - dtemp)) //temp higher than max set temp
    {
      digitalWrite(ledup, LOW); //cooling fan on
      delay(10);
    }

    if (getTemp() <= dtemp)  //temp lower or equal than min set temp
    {
      digitalWrite(ledup, HIGH); //cooling fan off
      delay(10);
    }

    if (getTemp() < dtemp - 0.1) // temp lower than 0.1 degrees-celsius below min set temp
    {
      digitalWrite(heat, LOW);   // heater on
      delay(5);
      state = digitalRead(heat);
    }

    if (getTemp() >= dtemp + 0.2)  //temp higher than 0.2 degrees-celsius above min set temp
    {
      digitalWrite(heat, HIGH);    //heater off
      delay(10);
      state = digitalRead(heat);
    }

    if (state == LOW)

    {
      lcd.setCursor(7, 0);
      lcd.print(char(1));
      lcd.setCursor(8, 0);
      lcd.print(char(2));
      delay(300);           // change sign
      lcd.setCursor(7, 0);
      lcd.print(char(2));   //  sign blink effect
      lcd.setCursor(8, 0);
      lcd.print(char(1));
      lcd.setCursor(9, 0);
      lcd.print(" ");
      delay(200);
    }

    if (state == HIGH)
    {
      lcd.setCursor(7, 0);
      lcd.print("   ");   // no sign heater
    }

    if (phValue > phset + 0.05)  // offset 0.05  pH is allowed to rise above the set pH value before before switching on co2 or led
    {
      digitalWrite(ledph, LOW);  // magnetvalve co2 open,(or led on in breadboard)
      delay(10);
      lcd.setCursor(11, 1);
      lcd.print(char(6));
      delay(5);
    }

    else if (phValue <= phset)
    {
      digitalWrite(ledph, HIGH); //magnetvalve co2 closed, (or led off in breadboard)
      delay(10);
      lcd.setCursor(11, 1);
      lcd.print(" ");
      delay(5);
    }
  }
}

float getTemp() {
  //returns the temperature from one DS18S20 in DEG Celsius
  byte data[12];
  byte addr[8];

  if ( !ds.search(addr)) {
    //no more sensors on chain, reset search
    ds.reset_search();
    return -1000;
  }

  if ( OneWire::crc8( addr, 7) != addr[7]) {
    //Serial.println("CRC is not valid!");
    return -1000;
  }

  if ( addr[0] != 0x10 && addr[0] != 0x28) {
    //Serial.print("Device is not recognized");
    return -1000;
  }

  ds.reset();
  ds.select(addr);
  ds.write(0x44, 1); // start conversion, with parasite power on at the end

  byte present = ds.reset();
  ds.select(addr);
  ds.write(0xBE); // Read Scratchpad

  for (int i = 0; i < 9; i++) { // we need 9 bytes
    data[i] = ds.read();
  }

  ds.reset_search();

  byte MSB = data[1];
  byte LSB = data[0];

  float tempRead = ((MSB << 8) | LSB); //using two's compliment
  float TemperatureSum = tempRead / 16;

  return TemperatureSum;
}

// code stored in the sketch: FishPiNo.ino
/*********************************************************************
   FishPiNo.ino
   Hardware platform   : Arduino Or Arduino Mega2560

   Description:
   Aquarium temperature (heating and cooling)) and pH-controller.
   Waterlevel indicator controls a cooling-fan, aquarium-heater and co2 system magnet valve.
   LCD Display for alert and views.

   Sensor pin:

   DIGITAL:
   LCD            : D2 - D3 - D4 - D5 - D11 - D12
   LEDUP          : D6  // led warning temp. upper limit or cooling Fan relais!
   WATERPIN       : D7  // floatswitch  for waterlevel
   LEDWATER       : D8  // warning led for water level
   DS18B20        : D9  // Signal pin on digital 9 temp sensor
   LEDPH          : D10 // led warning ph or relais for magnetic valve co2-system
   DHT22          : D13 // pin for DHT22

   ANALOG:
   dtempPin       : A1  //Lower temp.Limit pin with potmeter
   utempPin       : A2  //Upper temp.limit pin with potmeter
   SensorPin PH   : A3  //pH meter Analog output to Arduino Analog Input 3
   phsetPin       : A4  //set desired ph-value with potmeter
   HEATER         : A5  // led warning temp on  or RELAY FOR HEATER

   Free PIN:
   A0

   Author  :  nke69(nookie69@gmail.com)
   Version :  V1.0
   Date    :  31-03-2018

   Explanation :

   Controlling Aquarium temperature via heating and cooling relay, pH- controller and waterlevel indicator controls a cooling-fan,
   aquarium-heater and co2 system magnet valve.
   I used a 4 relay board, used 3 relay so you can do without the 3 leds.(those were for testing).
   Make sure the relay board has its own power-source (1x power adapter 12volt 1 amp,and 2x 7805 5 volt regulator.
   1x 7805 for arduino pro mini and sensors and and lcd, 1x 7805 for relay board.

   Parts list:

   1x arduino pro mini 16 mhz 5 volts with atmega 328.
   1x ph sensor  PH meterSKU: SEN0161, amplifier board included.
   1x DS18B20 one wire digital temperatur sensor, watersealed.
   1x 4 channel relais board.5 volts
   4x potentiometer 10 k for phset, maxtempset, mintempset and lcd-contrast.
   1x 16x2 lcd.
   1x power adapter 12 volt 1 amp.
   1x powerplug for housing to connect poweradapter to.
   2x 7805 volt regulator ,make a small pcb board with those two and the needed capacitors,to make 2 seperated 5 volts supplies, one for the relais board,one for the rest.
   1x led or blinkled for waterlevel warning indicator.
   1x 3 screw connector for temp sensor, 1x 2 screw connector for float switch sensor
   1x float sensor switch Water Level Liquid Sensor.
   2x build-on wall sockets ,both on 220 volts mains,here controlled by two relais,1 for heater and 1 for magnetvalve.
   1x pushbutton,connected to reset.

   Tips:

   Sometimes lcd can get scrambled because of the relais switching or the switching of my TL lighting, 1 push on //reset to fix it.
   a small condenator (100nF-10uF,trial and error) directly soldered over the lcd power pins(VSS and VDD) might help.
   if lcd is crambled the controller still work properly,lcd is just for indication!

 **********************************************************************/

#include <Adafruit_Sensor.h>
#include <LiquidCrystal.h>
#include <OneWire.h>
#include <SoftwareSerial.h>
#include "DHT.h"

#define VERSION "FishPiNo - V1.0"
#define DATEVER " du 30/03/2018 "


/*DS18S20 Signal pin on digital 9 temp sensor , change to your digital pin number*/
int DS18S20_Pin = 9;

#define DHTPIN 13     // what pin we're connected to

// Uncomment whatever type you're using!
//#define DHTTYPE DHT11   // DHT 11
#define DHTTYPE DHT22   // DHT 22  (AM2302)
//#define DHTTYPE DHT21   // DHT 21 (AM2301)

// Connect pin 1 (on the left) of the sensor to +5V
// Connect pin 2 of the sensor to whatever your DHTPIN is
// Connect pin 4 (on the right) of the sensor to GROUND
// Connect a 10K resistor from pin 2 (data) to pin 1 (power) of the sensor

DHT dht(DHTPIN, DHTTYPE);

// pins use for LCD16x2
LiquidCrystal lcd(12, 11, 5, 4, 3, 2);

int val, phset;
int state;

int utemp = 0, dtemp = 0, valup = 0, valdown = 0;
//Temperature chip i/o
OneWire ds(DS18S20_Pin);     // ds18b20 on digital pin 9
const int dtempPin = A1;     //Lower temp.Limit pin with potmeter
const int utempPin = A2;     //Upper temp.limit pin with potmeter
#define phsetPin A4          //set desired ph-value with potmeter
const int waterPin = 7;      //floatswitch  for waterlevel
const int ledup = 6;         //led warning temp. upper limit or cooling Fan relais!
const int ledph = 10;        //led warning ph or relais for magnetic valve co2-system
const int ledwater = 8;      //warning led for water level
const int heat = A5;         //relais heater element
#define SensorPin A3         //pH meter Analog output to Arduino Analog Input 3
#define Offset 0.0           //set your offset ph sensor here!!! shorted then ph=7 ,here mine gives 6.8 so offset = 0.2
unsigned long int avgValue;  //Store the average value of the sensor feedback
float b;
int buf[10], temp;
byte flame[8] = {
  B00100, B00100, B01110, B01010, B11011, B10001, B10001, B01110
};       //icon for flame
byte smalflame[8] = {
  B00000, B00000, B00100, B00100, B01110, B01010, B10001, B01110
};   //icon for small flame
byte thermometer[8] = {
  B00100, B01010, B01110, B01110, B11111, B11111, B11111, B01110
}; //icon thermometer
byte celsius[8] = {
  B11100, B10100, B11100, B00000, B00000, B00000, B00000, B00000
};     //icon celsius
byte tank[8] = {
  B01100, B00010, B00111, B01101, B10101, B10111, B10111, B00111
};        //icon co2 tank
byte co2[8] = {
  B00001, B00100, B10001, B00100, B01010, B00001, B00010, B00001
};         //icon c02 spray


void setup()
{
  Serial.begin(9600);
  lcd.begin(16, 2);
  lcd.setCursor(0, 0);
  lcd.createChar(1, flame);
  lcd.createChar(2, smalflame);
  lcd.createChar(3, thermometer);
  lcd.createChar(4, celsius);
  lcd.createChar(5, tank);
  lcd.createChar(6, co2);

  pinMode(ledup, OUTPUT);
  pinMode(ledph, OUTPUT);
  pinMode(heat, OUTPUT);
  pinMode(utempPin, INPUT);
  pinMode(dtempPin, INPUT);
  pinMode(phsetPin, INPUT);
  pinMode(waterPin, INPUT);
  pinMode(ledwater, OUTPUT);
  const int phsetPin = A4;
  int waterlevel;
  digitalWrite(ledup, HIGH);  // relais off !! depends on relais board you have.
  digitalWrite(ledph, HIGH);
  digitalWrite(heat, HIGH);
  state == HIGH ; // heat sign off
  dht.begin();
}

void loop()
{
  {
    float temperature = getTemp();                  // get temp from tempsensor
    utemp = analogRead(utempPin);                   // get max set temp from potmeter
    dtemp = analogRead(dtempPin);                   // get min set temp from potmeter
    float phset = analogRead(phsetPin);             // get desired ph value from potmeter

    utemp = map(utemp, 0, 1023, 19, 31);            // you can change 19 and 31 to your desired temp range for the set potmeter
    dtemp = map(dtemp, 0, 1023, 19, 31);            // idem
    phset = map(phset, 0.0, 1023.0, 10.0, 140.0);   // give the ph value
    phset = (phset / 10);                           // with 1 decimal
    for (int i = 0; i < 10; i++)                    //Get 10 sample value from the sensor for smooth the value
    {
      buf[i] = analogRead(SensorPin);
      delay(10);
    }
    for (int i = 0; i < 9; i++) //sort the analog from small to large
    {
      for (int j = i + 1; j < 10; j++)
      {
        if (buf[i] > buf[j])
        {
          temp = buf[i];
          buf[i] = buf[j];
          buf[j] = temp;
        }
      }
    }

    // Reading temperature or humidity takes about 250 milliseconds!
    // Sensor readings may also be up to 2 seconds 'old' (its a very slow sensor)
    float hum = dht.readHumidity();
    float temp = dht.readTemperature();



    avgValue = 0;
    for (int i = 2; i < 8; i++)                       //take the average value of 6 center sample
      avgValue += buf[i];
    float phValue = (float)avgValue * 5.0 / 1024 / 6; //convert the analog into millivolt
    phValue = 3.5 * phValue + Offset;                 //convert the millivolt into pH value

    int waterlevel;
    waterlevel = digitalRead(waterPin);

    if (waterlevel == HIGH)
    {

      digitalWrite(ledwater, HIGH);     //led on ,i used a blinkled
      lcd.setCursor(0, 1);
      lcd.print("^^^NIVEAU EAU^^^");    // water (niveau=)level  ,total of 16 characters incluiding tab
      delay(500);                       // change switchingspeed to your liking
      lcd.setCursor(0, 1);              // replace on same position
      lcd.print("____TROP BAS____");    // low  ,again total of 16 characters
      Serial.print(getTemp(), 1);
      Serial.print(" \t"); //tab
      Serial.print(phValue, 1);
      Serial.print(" \t"); //tab
      Serial.print(waterlevel);
      Serial.print(" \t"); //tab
      Serial.print(hum);
      Serial.print(" \t"); //tab
      Serial.println(temp);
      delay(3000);                       // again change to your liking
    }
    else
    {
      digitalWrite(ledwater, LOW); //led off
      lcd.setCursor(0, 0);
      lcd.print(char(3));
      lcd.setCursor(1, 0);
      lcd.print(getTemp(), 1);    // temp with 1 decimal
      lcd.setCursor(5, 0);
      lcd.print(char(4));
      lcd.setCursor(6, 0);
      lcd.print("C");
      lcd.setCursor(10, 0);
      lcd.print("pH:");
      lcd.setCursor(13, 0);
      lcd.print(phValue, 1);      // ph value with 1 decimal
      lcd.setCursor(7, 1);
      lcd.print(utemp);           //max set temp,no decimal
      lcd.setCursor(4, 1);
      lcd.print(" ");
      lcd.setCursor(0, 1);
      lcd.print("L~");            // L from Low set temp with arrow right
      lcd.setCursor(2, 1);
      lcd.print(dtemp);           //min set temp ,no decimal
      lcd.setCursor(12, 1);
      lcd.print("~");             //this sign gives on my lcd an arrow to the right
      lcd.setCursor(5, 1);
      lcd.print("H~");            //H from High set temp with arrow right
      lcd.setCursor(13, 1);
      lcd.print(phset, 1);        //ph set value with 1 decimal
      lcd.setCursor(9, 1);
      lcd.print(" ");
      lcd.setCursor(10, 1);
      lcd.print(char(5));
      delay(3000);               // Rafraichissement des donnees
      Serial.print(getTemp(), 1);
      Serial.print(" \t"); //tab
      Serial.print(phValue, 1);
      Serial.print(" \t"); //tab
      Serial.print(waterlevel);
      Serial.print(" \t"); //tab

      // check if returns are valid, if they are NaN (not a number) then something went wrong!
      if (isnan(temp) || isnan(hum)) {
        Serial.println("Failed to read from DHT");
      }
      else {
        Serial.print(hum);
        Serial.print(" \t"); //tab
        Serial.println(temp);
      }

      state = digitalRead(heat); // read the state of the heater-relais(when reset,the heatersign would turn on while heater is off.This gives the right indication.)
    }

    if (getTemp() > dtemp + (utemp - dtemp)) //temp higher than max set temp
    {
      digitalWrite(ledup, LOW); //cooling fan on
      delay(10);
    }

    if (getTemp() <= dtemp)  //temp lower or equal than min set temp
    {
      digitalWrite(ledup, HIGH); //cooling fan off
      delay(10);
    }

    if (getTemp() < dtemp - 0.1) // temp lower than 0.1 degrees-celsius below min set temp
    {
      digitalWrite(heat, LOW);   // heater on
      delay(5);
      state = digitalRead(heat);
    }

    if (getTemp() >= dtemp + 0.2)  //temp higher than 0.2 degrees-celsius above min set temp
    {
      digitalWrite(heat, HIGH);    //heater off
      delay(10);
      state = digitalRead(heat);
    }

    if (state == LOW)

    {
      lcd.setCursor(7, 0);
      lcd.print(char(1));
      lcd.setCursor(8, 0);
      lcd.print(char(2));
      delay(300);           // change sign
      lcd.setCursor(7, 0);
      lcd.print(char(2));   //  sign blink effect
      lcd.setCursor(8, 0);
      lcd.print(char(1));
      lcd.setCursor(9, 0);
      lcd.print(" ");
      delay(200);
    }

    if (state == HIGH)
    {
      lcd.setCursor(7, 0);
      lcd.print("   ");   // no sign heater
    }

    if (phValue > phset + 0.05)  // offset 0.05  pH is allowed to rise above the set pH value before before switching on co2 or led
    {
      digitalWrite(ledph, LOW);  // magnetvalve co2 open,(or led on in breadboard)
      delay(10);
      lcd.setCursor(11, 1);
      lcd.print(char(6));
      delay(5);
    }

    else if (phValue <= phset)
    {
      digitalWrite(ledph, HIGH); //magnetvalve co2 closed, (or led off in breadboard)
      delay(10);
      lcd.setCursor(11, 1);
      lcd.print(" ");
      delay(5);
    }
  }
}

float getTemp() {
  //returns the temperature from one DS18S20 in DEG Celsius
  byte data[12];
  byte addr[8];

  if ( !ds.search(addr)) {
    //no more sensors on chain, reset search
    ds.reset_search();
    return -1000;
  }

  if ( OneWire::crc8( addr, 7) != addr[7]) {
    //Serial.println("CRC is not valid!");
    return -1000;
  }

  if ( addr[0] != 0x10 && addr[0] != 0x28) {
    //Serial.print("Device is not recognized");
    return -1000;
  }

  ds.reset();
  ds.select(addr);
  ds.write(0x44, 1); // start conversion, with parasite power on at the end

  byte present = ds.reset();
  ds.select(addr);
  ds.write(0xBE); // Read Scratchpad

  for (int i = 0; i < 9; i++) { // we need 9 bytes
    data[i] = ds.read();
  }

  ds.reset_search();

  byte MSB = data[1];
  byte LSB = data[0];

  float tempRead = ((MSB << 8) | LSB); //using two's compliment
  float TemperatureSum = tempRead / 16;

  return TemperatureSum;
}
